# Fritzing sketch ledstrip_artproject (saved by Fritzing 0.9.3b)

parts:
  Part1 = Arduino Mega 2560 (Rev3)
  Part2 = Arduino Mega 2560 (Rev3)
  IR1 = TSOP312.., 314.. [package=THT]
  RGB_SMD_LED1 = SMD RGB LED (WS2812) [package=5050]
  RGB_SMD_LED2 = SMD RGB LED (WS2812) [package=5050]
  RGB_SMD_LED3 = SMD RGB LED (WS2812) [package=5050]
  RGB_SMD_LED4 = SMD RGB LED (WS2812) [package=5050]

nets:
  N1: Part1.5V, IR1.Data
  N2: Part1.GND, IR1.Vs
  N3: Part1.D2_PWM, IR1.GND
  N4: Part2.D47, RGB_SMD_LED1.DIn
  N5: Part2.D49, RGB_SMD_LED2.DIn
  N6: Part2.D51, RGB_SMD_LED3.DIn
  N7: Part2.D53, RGB_SMD_LED4.DIn
